// Logisim project FullSystem_v3.circ as structural Verilog: 1 circuit, main circuit main
module main (
  input  RST,
  input  A3,
  input  A2,
  input  A1,
  input  A0,
  input  I3,
  input  I2,
  input  I1,
  input  I0,
  input  in_10,
  input  in_11,
  input  in_12,
  input  in_13,
  input  in_14,
  input  in_15,
  input  in_16,
  input  in_17,
  input  in_18,
  input  in_19,
  input  in_20,
  input  in_21,
  input  in_22,
  input  in_23,
  output DATA,
  output DATA_2,
  output CLK_1,
  output CLK_2,
  output CLK_2_2,
  output out_29,
  output IEN,
  output OEN,
  output _2_WRITE,
  output out_33,
  output _15_RR,
  output CAR,
  output out_36,
  output RR,
  output out_38,
  output SKIP,
  output _10_FLG0,
  output _12_JMP,
  output _11_RTN,
  output _9_FLGF,
  output out_44,
  output out_45,
  output out_46,
  output out_47,
  output OUTPUT,
  output out_49,
  output out_50,
  output out_51
);

  wire buffer_1_out, buffer_2_out, buffer_3_out, buffer_4_out, buffer_5_out, buffer_6_out, buffer_7_out,
       buffer_8_out, buffer_9_out, buffer_10_out, buffer_11_out, buffer_12_out, buffer_13_out, buffer_17_out,
       buffer_18_out, buffer_19_out, buffer_20_out, buffer_21_out, buffer_22_out, buffer_23_out,
       buffer_24_out, buffer_25_out, buffer_26_out, buffer_27_out, buffer_30_out, buffer_31_out,
       buffer_32_out, buffer_33_out, buffer_36_out, buffer_37_out, buffer_40_out, buffer_45_out,
       buffer_46_out, buffer_48_out, clock_1_out, d_ff_1_q, d_ff_2_qn, d_ff_3_q, nand_1_out, nand_2_out,
       nand_3_out, nand_4_out, nand_5_out, nand_6_out, nand_7_out, nand_8_out, nand_9_out, nand_10_out,
       nand_11_out, nand_12_out, nand_13_out, nand_14_out, nand_15_out, nand_16_out, nor_1_out, nor_2_out,
       nor_3_out, nor_4_out, nor_5_out, nor_6_out, nor_7_out, nor_8_out, nor_9_out, nor_10_out, nor_11_out,
       nor_12_out, nor_13_out, nor_14_out, nor_15_out, nor_16_out, nor_18_out, nor_20_out, nor_22_out,
       nor_24_out, nor_25_out, nor_26_out, nor_27_out, nor_28_out, nor_29_out, nor_30_out, nor_31_out,
       nor_32_out, nor_33_out, nor_34_out, nor_35_out, nor_36_out, nor_37_out, nor_38_out, nor_39_out,
       nor_40_out, nor_41_out, nor_42_out, nor_43_out, nor_44_out, nor_45_out, nor_46_out, nor_47_out,
       nor_48_out, nor_49_out, nor_50_out, nor_51_out, nor_52_out, nor_53_out, nor_54_out, nor_55_out,
       nor_56_out, nor_57_out, nor_58_out, nor_59_out, nor_60_out, nor_61_out, nor_62_out, nor_63_out,
       nor_64_out, nor_65_out, nor_66_out, nor_67_out, nor_68_out, nor_69_out, nor_70_out, nor_71_out,
       nor_72_out, nor_73_out, nor_74_out, nor_75_out, nor_76_out, nor_77_out, nor_78_out, nor_79_out,
       nor_80_out, nor_81_out, nor_82_out, nor_83_out, nor_84_out, nor_85_out, nor_86_out, nor_87_out,
       nor_88_out, nor_89_out, nor_90_out, nor_91_out, nor_92_out, nor_93_out, nor_94_out, nor_95_out,
       nor_96_out, nor_97_out, nor_98_out, nor_99_out, nor_100_out, nor_101_out, nor_103_out, nor_104_out,
       nor_105_out, nor_106_out, nor_107_out, nor_108_out, nor_109_out, nor_110_out, nor_111_out,
       nor_112_out, nor_113_out, nor_114_out, nor_115_out, nor_116_out, nor_117_out, nor_118_out,
       nor_119_out, nor_120_out, nor_121_out, nor_122_out, nor_123_out, nor_124_out, nor_125_out,
       nor_126_out, nor_127_out, nor_128_out, nor_129_out, nor_130_out, nor_131_out, nor_132_out,
       nor_133_out, nor_134_out, nor_135_out, nor_136_out, nor_137_out, nor_138_out, nor_139_out,
       nor_140_out, nor_141_out, nor_142_out, nor_143_out, nor_144_out, nor_145_out, nor_146_out,
       nor_147_out, nor_148_out, nor_149_out, nor_150_out, nor_151_out, nor_152_out, nor_153_out,
       nor_154_out, nor_155_out, nor_156_out, nor_157_out, nor_158_out, nor_159_out, nor_160_out,
       nor_161_out, nor_162_out, nor_163_out, nor_164_out, nor_165_out, nor_166_out, nor_167_out,
       nor_168_out, nor_170_out, nor_171_out, nor_172_out, nor_173_out, nor_174_out, nor_176_out, not_1_out,
       not_2_out, not_3_out, not_4_out, not_6_out, not_7_out, not_8_out, not_9_out, not_10_out, not_11_out,
       not_12_out, not_13_out, not_14_out, not_15_out, not_16_out, not_17_out, not_18_out, not_19_out,
       not_20_out, not_21_out, or_1_out, or_2_out, or_3_out, or_4_out, or_5_out, or_6_out, or_7_out,
       or_8_out, or_9_out, or_10_out, or_11_out, or_12_out, or_13_out, or_14_out, or_15_out, or_16_out,
       or_17_out, or_18_out, or_19_out, or_20_out, or_21_out, or_22_out, or_23_out, or_24_out, or_25_out,
       or_26_out, or_27_out, or_28_out, or_29_out, or_30_out, or_31_out, or_32_out, or_33_out, or_34_out,
       or_35_out, or_36_out, or_37_out, or_38_out, or_39_out, or_40_out, or_41_out, or_42_out, or_43_out,
       or_44_out, or_45_out, or_46_out, or_47_out, or_48_out, or_49_out, or_50_out, or_51_out, or_52_out,
       or_53_out, or_54_out, or_55_out, or_56_out, or_57_out, or_58_out, or_59_out, or_61_out, or_62_out,
       or_63_out, or_64_out, or_65_out, or_66_out;
  wire [7:0] counter_1_q, rom_1_data;

  or or_1 (or_1_out, A2, rom_1_data[6]);
  or or_2 (or_2_out, A3, rom_1_data[7]);
  or or_3 (or_3_out, A1, rom_1_data[5]);
  or or_4 (or_4_out, A0, rom_1_data[4]);
  or or_5 (or_5_out, I3, rom_1_data[3]);
  not not_1 (not_1_out, or_3_out);
  not not_2 (not_2_out, or_1_out);
  or or_6 (or_6_out, I1, rom_1_data[1]);
  or or_7 (or_7_out, I2, rom_1_data[2]);
  or or_8 (or_8_out, or_20_out, buffer_48_out);
  or or_9 (or_9_out, or_6_out, buffer_48_out);
  or or_10 (or_10_out, or_7_out, buffer_48_out);
  or or_11 (or_11_out, buffer_48_out, or_5_out);
  not not_3 (not_3_out, or_4_out);
  or or_12 (or_12_out, or_4_out, or_3_out, or_1_out);
  or or_13 (or_13_out, not_3_out, or_3_out, or_1_out);
  or or_14 (or_14_out, or_4_out, not_1_out, or_1_out);
  or or_15 (or_15_out, not_3_out, not_1_out, or_1_out);
  or or_16 (or_16_out, or_4_out, or_3_out, not_2_out);
  or or_17 (or_17_out, not_3_out, or_3_out, not_2_out);
  or or_18 (or_18_out, or_4_out, not_1_out, not_2_out);
  or or_19 (or_19_out, not_3_out, not_1_out, not_2_out);
  or or_20 (or_20_out, I0, rom_1_data[0]);
  buf buffer_1 (buffer_1_out, or_8_out);
  buf buffer_2 (buffer_2_out, or_9_out);
  buf buffer_3 (buffer_3_out, or_10_out);
  buf buffer_4 (buffer_4_out, or_11_out);
  not not_4 (not_4_out, or_2_out);
  nor nor_1 (nor_1_out, nor_4_out, nor_2_out);
  nor nor_2 (nor_2_out, nor_1_out, CLK_1);
  nor nor_3 (nor_3_out, nor_2_out, CLK_1, nor_4_out);
  nor nor_4 (nor_4_out, nor_3_out, buffer_1_out);
  nor nor_5 (nor_5_out, nor_8_out, nor_6_out);
  nor nor_6 (nor_6_out, nor_5_out, CLK_1);
  nor nor_7 (nor_7_out, nor_6_out, CLK_1, nor_8_out);
  nor nor_8 (nor_8_out, nor_7_out, buffer_2_out);
  nor nor_9 (nor_9_out, nor_12_out, nor_10_out);
  nor nor_10 (nor_10_out, nor_9_out, CLK_1);
  nor nor_11 (nor_11_out, nor_10_out, CLK_1, nor_12_out);
  nor nor_12 (nor_12_out, nor_11_out, buffer_3_out);
  nor nor_13 (nor_13_out, nor_16_out, nor_14_out);
  nor nor_14 (nor_14_out, nor_13_out, CLK_1);
  nor nor_15 (nor_15_out, nor_14_out, CLK_1, nor_16_out);
  nor nor_16 (nor_16_out, nor_15_out, buffer_4_out);
  or or_21 (or_21_out, RST, nor_2_out);
  nor nor_17 (out_29, or_21_out, nor_18_out);
  nor nor_18 (nor_18_out, out_29, nor_3_out);
  or or_22 (or_22_out, RST, nor_6_out);
  nor nor_19 (out_33, or_22_out, nor_20_out);
  nor nor_20 (nor_20_out, out_33, nor_7_out);
  or or_23 (or_23_out, RST, nor_10_out);
  nor nor_21 (out_36, or_23_out, nor_22_out);
  nor nor_22 (nor_22_out, out_36, nor_11_out);
  or or_24 (or_24_out, RST, nor_14_out);
  nor nor_23 (out_38, or_24_out, nor_24_out);
  nor nor_24 (nor_24_out, out_38, nor_15_out);
  or or_25 (or_25_out, buffer_33_out, or_13_out, or_2_out);
  or or_26 (or_26_out, buffer_33_out, or_12_out, or_2_out);
  or or_27 (or_27_out, buffer_33_out, or_13_out, not_4_out);
  or or_28 (or_28_out, buffer_33_out, or_12_out, not_4_out);
  nor nor_25 (nor_25_out, not_4_out, or_12_out, buffer_45_out);
  nor nor_26 (nor_26_out, in_10, in_17);
  buf buffer_5 (buffer_5_out, out_29);
  buf buffer_6 (buffer_6_out, nor_18_out);
  buf buffer_7 (buffer_7_out, out_33);
  buf buffer_8 (buffer_8_out, nor_20_out);
  buf buffer_9 (buffer_9_out, out_36);
  buf buffer_10 (buffer_10_out, nor_22_out);
  buf buffer_11 (buffer_11_out, out_38);
  buf buffer_12 (buffer_12_out, nor_24_out);
  nor nor_27 (nor_27_out, buffer_13_out, or_25_out);
  nor nor_28 (nor_28_out, nor_27_out, or_25_out);
  nor nor_29 (nor_29_out, buffer_13_out, or_26_out);
  nor nor_30 (nor_30_out, nor_29_out, or_26_out);
  nor nor_31 (nor_31_out, buffer_13_out, or_27_out);
  nor nor_32 (nor_32_out, nor_31_out, or_27_out);
  nor nor_33 (nor_33_out, buffer_13_out, or_28_out);
  nor nor_34 (nor_34_out, nor_33_out, or_28_out);
  nor nor_35 (nor_35_out, not_4_out, nor_26_out, or_13_out);
  nor nor_36 (nor_36_out, in_11, in_18);
  Clock clock_1 (.out(clock_1_out));
  D_Flip_Flop d_ff_1 (.clk(clock_1_out), .D(d_ff_2_qn), .Q(d_ff_1_q), .reset(d_ff_3_q));  // open: Qn, preset, en
  not not_5 (CLK_1, d_ff_1_q);
  buf buffer_13 (buffer_13_out, DATA);
  nor nor_37 (nor_37_out, nor_27_out, nor_38_out);
  nor nor_38 (nor_38_out, nor_37_out, nor_28_out);
  nor nor_39 (nor_39_out, nor_29_out, nor_40_out);
  nor nor_40 (nor_40_out, nor_39_out, nor_30_out);
  nor nor_41 (nor_41_out, nor_31_out, nor_42_out);
  nor nor_42 (nor_42_out, nor_41_out, nor_32_out);
  nor nor_43 (nor_43_out, nor_33_out, nor_44_out);
  nor nor_44 (nor_44_out, nor_43_out, nor_34_out);
  nor nor_45 (nor_45_out, not_4_out, nor_36_out, or_14_out);
  nor nor_46 (nor_46_out, in_12, in_19);
  D_Flip_Flop d_ff_2 (
    .clk(clock_1_out), .D(d_ff_1_q), .Q(CLK_2), .Qn(d_ff_2_qn), .reset(d_ff_3_q));  // open: preset, en
  nor nor_47 (nor_47_out, buffer_32_out, nor_38_out, or_13_out, or_2_out);
  nor nor_48 (nor_48_out, buffer_32_out, nor_40_out, or_12_out, or_2_out);
  buf buffer_14 (OUTPUT, nor_41_out);
  buf buffer_15 (out_44, nor_43_out);
  or or_29 (or_29_out, nor_25_out, nor_35_out, nor_45_out);
  nor nor_49 (nor_49_out, not_4_out, nor_46_out, or_15_out);
  nor nor_50 (nor_50_out, in_13, in_20);
  D_Flip_Flop d_ff_3 (.clk(clock_1_out), .D(CLK_2), .Q(d_ff_3_q));  // open: Qn, preset, en, reset
  buf buffer_16 (_10_FLG0, nor_51_out);
  nor nor_51 (nor_51_out, buffer_5_out, buffer_7_out, buffer_9_out, buffer_11_out);
  nor nor_52 (nor_52_out, buffer_6_out, buffer_7_out, buffer_9_out, buffer_11_out);
  buf buffer_17 (buffer_17_out, nor_52_out);
  nor nor_53 (nor_53_out, buffer_5_out, buffer_8_out, buffer_9_out, buffer_11_out);
  buf buffer_18 (buffer_18_out, nor_53_out);
  buf buffer_19 (buffer_19_out, nor_54_out);
  nor nor_54 (nor_54_out, buffer_6_out, buffer_8_out, buffer_9_out, buffer_11_out);
  nor nor_55 (nor_55_out, buffer_5_out, buffer_7_out, buffer_10_out, buffer_11_out);
  buf buffer_20 (buffer_20_out, nor_55_out);
  buf buffer_21 (buffer_21_out, nor_56_out);
  nor nor_56 (nor_56_out, buffer_6_out, buffer_7_out, buffer_10_out, buffer_11_out);
  nor nor_57 (nor_57_out, buffer_5_out, buffer_8_out, buffer_10_out, buffer_11_out);
  buf buffer_22 (buffer_22_out, nor_57_out);
  nor nor_58 (nor_58_out, buffer_6_out, buffer_8_out, buffer_10_out, buffer_11_out);
  buf buffer_23 (buffer_23_out, nor_58_out);
  buf buffer_24 (buffer_24_out, nor_59_out);
  nor nor_59 (nor_59_out, buffer_5_out, buffer_7_out, buffer_9_out, buffer_12_out);
  nor nor_60 (nor_60_out, buffer_6_out, buffer_7_out, buffer_9_out, buffer_12_out);
  buf buffer_25 (buffer_25_out, nor_60_out);
  buf buffer_26 (buffer_26_out, nor_61_out);
  nor nor_61 (nor_61_out, buffer_5_out, buffer_8_out, buffer_9_out, buffer_12_out);
  nor nor_62 (nor_62_out, buffer_6_out, buffer_8_out, buffer_9_out, buffer_12_out);
  buf buffer_27 (buffer_27_out, nor_62_out);
  nor nor_63 (nor_63_out, buffer_5_out, buffer_7_out, buffer_10_out, buffer_12_out);
  buf buffer_28 (_12_JMP, nor_63_out);
  buf buffer_29 (_11_RTN, nor_64_out);
  nor nor_64 (nor_64_out, buffer_6_out, buffer_7_out, buffer_10_out, buffer_12_out);
  nor nor_65 (nor_65_out, buffer_5_out, buffer_8_out, buffer_10_out, buffer_12_out);
  buf buffer_30 (buffer_30_out, nor_65_out);
  buf buffer_31 (buffer_31_out, nor_66_out);
  nor nor_66 (nor_66_out, buffer_6_out, buffer_8_out, buffer_10_out, buffer_12_out);
  or or_30 (or_30_out, buffer_33_out, or_15_out, or_2_out);
  or or_31 (or_31_out, buffer_33_out, or_14_out, or_2_out);
  or or_32 (or_32_out, buffer_33_out, or_15_out, not_4_out);
  or or_33 (or_33_out, buffer_33_out, or_14_out, not_4_out);
  nor nor_67 (nor_67_out, not_4_out, nor_50_out, or_16_out);
  nor nor_68 (nor_68_out, in_14, in_21);
  buf buffer_32 (buffer_32_out, _2_WRITE);
  buf buffer_33 (buffer_33_out, nand_16_out);
  nor nor_69 (nor_69_out, buffer_13_out, or_30_out);
  nor nor_70 (nor_70_out, nor_69_out, or_30_out);
  nor nor_71 (nor_71_out, buffer_13_out, or_31_out);
  nor nor_72 (nor_72_out, nor_71_out, or_31_out);
  nor nor_73 (nor_73_out, buffer_13_out, or_32_out);
  nor nor_74 (nor_74_out, nor_73_out, or_32_out);
  nor nor_75 (nor_75_out, buffer_13_out, or_33_out);
  nor nor_76 (nor_76_out, nor_75_out, or_33_out);
  or or_34 (or_34_out, or_29_out, nor_49_out, nor_67_out);
  nor nor_77 (nor_77_out, not_4_out, nor_68_out, or_17_out);
  nor nor_78 (nor_78_out, in_15, in_22);
  nand nand_1 (nand_1_out, buffer_26_out, CLK_2);
  nor nor_79 (nor_79_out, nor_69_out, nor_80_out);
  nor nor_80 (nor_80_out, nor_79_out, nor_70_out);
  nor nor_81 (nor_81_out, nor_71_out, nor_82_out);
  nor nor_82 (nor_82_out, nor_81_out, nor_72_out);
  nor nor_83 (nor_83_out, nor_73_out, nor_84_out);
  buf buffer_34 (out_49, nor_83_out);
  nor nor_84 (nor_84_out, nor_83_out, nor_74_out);
  nor nor_85 (nor_85_out, nor_75_out, nor_86_out);
  buf buffer_35 (out_45, nor_85_out);
  nor nor_86 (nor_86_out, nor_85_out, nor_76_out);
  nor nor_87 (nor_87_out, not_4_out, nor_78_out, or_18_out);
  nor nor_88 (nor_88_out, in_16, in_23);
  Counter counter_1 (.Q(counter_1_q), .clk(d_ff_3_q), .clr(RST));  // open: load, D, count, carry
  nor nor_89 (nor_89_out, nor_92_out, nor_90_out);
  nor nor_90 (nor_90_out, nor_89_out, nand_1_out);
  nor nor_91 (nor_91_out, nor_90_out, nand_1_out, nor_92_out);
  nor nor_92 (nor_92_out, nor_91_out, DATA);
  nor nor_93 (nor_93_out, buffer_37_out, buffer_19_out);
  not not_6 (not_6_out, buffer_37_out);
  nor nor_94 (nor_94_out, buffer_32_out, nor_80_out, or_15_out, or_2_out);
  nor nor_95 (nor_95_out, buffer_32_out, nor_82_out, or_14_out, or_2_out);
  or or_35 (or_35_out, or_34_out, nor_77_out, nor_87_out);
  nor nor_96 (nor_96_out, not_4_out, nor_88_out, or_19_out);
  or or_36 (or_36_out, RST, nor_90_out);
  nor nor_97 (nor_97_out, buffer_37_out, nor_93_out);
  or or_37 (or_37_out, nor_97_out, nor_98_out);
  nor nor_98 (nor_98_out, nor_93_out, buffer_19_out);
  nand nand_2 (nand_2_out, buffer_37_out, buffer_17_out);
  nor nor_99 (nor_99_out, buffer_21_out, buffer_37_out, RR);
  nor nor_100 (nor_100_out, buffer_21_out, buffer_37_out, RR);
  nor nor_101 (nor_101_out, buffer_22_out, not_6_out, buffer_45_out);
  or or_38 (or_38_out, buffer_21_out, buffer_22_out, buffer_23_out);
  or or_39 (or_39_out, buffer_33_out, or_17_out, or_2_out);
  or or_40 (or_40_out, buffer_33_out, or_16_out, or_2_out);
  or or_41 (or_41_out, buffer_33_out, or_17_out, not_4_out);
  or or_42 (or_42_out, buffer_33_out, or_16_out, not_4_out);
  or or_43 (or_43_out, or_35_out, nor_96_out);
  ROM rom_1 (.addr(counter_1_q), .data(rom_1_data));  // open: sel
  nor nor_102 (IEN, or_36_out, nor_103_out);
  nor nor_103 (nor_103_out, IEN, nor_91_out);
  buf buffer_36 (buffer_36_out, or_37_out);
  not not_7 (not_7_out, nand_2_out);
  nor nor_104 (nor_104_out, nor_99_out, nor_100_out, nor_101_out);
  nor nor_105 (nor_105_out, buffer_13_out, or_39_out);
  nor nor_106 (nor_106_out, nor_105_out, or_39_out);
  nor nor_107 (nor_107_out, buffer_13_out, or_40_out);
  nor nor_108 (nor_108_out, nor_107_out, or_40_out);
  nor nor_109 (nor_109_out, buffer_13_out, or_41_out);
  nor nor_110 (nor_110_out, nor_109_out, or_41_out);
  nor nor_111 (nor_111_out, buffer_13_out, or_42_out);
  nor nor_112 (nor_112_out, nor_111_out, or_42_out);
  nand nand_3 (nand_3_out, DATA, IEN);
  not not_8 (not_8_out, nand_3_out);
  buf buffer_37 (buffer_37_out, not_8_out);
  nor nor_113 (nor_113_out, RR, buffer_36_out);
  nor nor_114 (nor_114_out, not_10_out, nor_113_out);
  nand nand_4 (nand_4_out, nor_131_out, or_44_out);
  or or_44 (or_44_out, buffer_19_out, buffer_18_out);
  or or_45 (or_45_out, not_7_out, buffer_20_out);
  not not_9 (not_9_out, nand_5_out);
  nand nand_5 (nand_5_out, nor_104_out, or_38_out);
  or or_46 (or_46_out, buffer_21_out, buffer_22_out, buffer_23_out);
  or or_47 (or_47_out, buffer_17_out, buffer_19_out, buffer_18_out);
  nor nor_115 (nor_115_out, nor_105_out, nor_116_out);
  nor nor_116 (nor_116_out, nor_115_out, nor_106_out);
  nor nor_117 (nor_117_out, nor_107_out, nor_118_out);
  nor nor_118 (nor_118_out, nor_117_out, nor_108_out);
  nor nor_119 (nor_119_out, nor_109_out, nor_120_out);
  buf buffer_38 (out_50, nor_119_out);
  nor nor_120 (nor_120_out, nor_119_out, nor_110_out);
  nor nor_121 (nor_121_out, nor_111_out, nor_122_out);
  buf buffer_39 (out_46, nor_121_out);
  nor nor_122 (nor_122_out, nor_121_out, nor_112_out);
  nand nand_6 (nand_6_out, CLK_2, or_48_out);
  or or_48 (or_48_out, buffer_18_out, buffer_19_out, buffer_20_out);
  not not_10 (not_10_out, nand_7_out);
  nand nand_7 (nand_7_out, RR, buffer_36_out);
  nand nand_8 (nand_8_out, nor_114_out, CAR);
  nor nor_123 (nor_123_out, nor_114_out, CAR);
  not not_11 (not_11_out, nand_4_out);
  nor nor_124 (nor_124_out, or_49_out, nor_125_out);
  nor nor_125 (nor_125_out, or_49_out, RR);
  or or_49 (or_49_out, or_46_out, or_47_out);
  nor nor_126 (nor_126_out, buffer_32_out, nor_116_out, or_17_out, or_2_out);
  nor nor_127 (nor_127_out, buffer_32_out, nor_118_out, or_16_out, or_2_out);
  buf buffer_40 (buffer_40_out, nand_6_out);
  not not_12 (not_12_out, buffer_40_out);
  or or_50 (or_50_out, not_10_out, not_13_out);
  not not_13 (not_13_out, nand_8_out);
  or or_51 (or_51_out, not_11_out, or_45_out, not_9_out, nor_124_out);
  not not_14 (not_14_out, CLK_2);
  or or_52 (or_52_out, buffer_33_out, or_19_out, or_2_out);
  or or_53 (or_53_out, buffer_33_out, or_18_out, or_2_out);
  or or_54 (or_54_out, buffer_33_out, or_19_out, not_4_out);
  or or_55 (or_55_out, buffer_33_out, or_18_out, not_4_out);
  nor nor_128 (nor_128_out, nor_144_out, buffer_40_out);
  nor nor_129 (nor_129_out, nor_128_out, buffer_40_out);
  nor nor_130 (nor_130_out, buffer_20_out, or_50_out);
  nor nor_131 (nor_131_out, not_13_out, nor_123_out);
  nor nor_132 (nor_132_out, or_51_out, not_14_out);
  nor nor_133 (nor_133_out, nor_132_out, not_14_out);
  nor nor_134 (nor_134_out, buffer_13_out, or_52_out);
  nor nor_135 (nor_135_out, nor_134_out, or_52_out);
  nor nor_136 (nor_136_out, buffer_13_out, or_53_out);
  nor nor_137 (nor_137_out, nor_136_out, or_53_out);
  nor nor_138 (nor_138_out, buffer_13_out, or_54_out);
  nor nor_139 (nor_139_out, nor_138_out, or_54_out);
  nor nor_140 (nor_140_out, buffer_13_out, or_55_out);
  nor nor_141 (nor_141_out, nor_140_out, or_55_out);
  nor nor_142 (nor_142_out, nor_128_out, nor_143_out);
  nor nor_143 (nor_143_out, nor_142_out, nor_129_out);
  nor nor_144 (nor_144_out, buffer_20_out, nor_130_out);
  nor nor_145 (nor_145_out, nor_132_out, nor_146_out);
  nor nor_146 (nor_146_out, nor_145_out, nor_133_out);
  or or_56 (or_56_out, buffer_30_out, _11_RTN);
  nor nor_147 (nor_147_out, nor_134_out, nor_148_out);
  nor nor_148 (nor_148_out, nor_147_out, nor_135_out);
  nor nor_149 (nor_149_out, nor_136_out, nor_150_out);
  nor nor_150 (nor_150_out, nor_149_out, nor_137_out);
  nor nor_151 (nor_151_out, nor_138_out, nor_152_out);
  buf buffer_41 (out_51, nor_151_out);
  nor nor_152 (nor_152_out, nor_151_out, nor_139_out);
  nor nor_153 (nor_153_out, nor_140_out, nor_154_out);
  buf buffer_42 (out_47, nor_153_out);
  nor nor_154 (nor_154_out, nor_153_out, nor_141_out);
  nor nor_155 (nor_155_out, nor_142_out, not_12_out);
  nor nor_156 (nor_156_out, nor_155_out, not_12_out);
  nor nor_157 (nor_157_out, nor_145_out, CLK_2);
  nor nor_158 (nor_158_out, nor_157_out, CLK_2);
  or or_57 (or_57_out, _11_RTN, buffer_45_out);
  nand nand_9 (nand_9_out, or_57_out, or_56_out, nor_170_out);
  nor nor_159 (nor_159_out, buffer_32_out, nor_148_out, or_19_out, or_2_out);
  nor nor_160 (nor_160_out, buffer_32_out, nor_150_out, or_18_out, or_2_out);
  nor nor_161 (nor_161_out, nor_155_out, nor_162_out);
  nor nor_162 (nor_162_out, nor_161_out, nor_156_out);
  buf buffer_43 (CAR, nor_161_out);
  nor nor_163 (nor_163_out, nor_157_out, nor_164_out);
  buf buffer_44 (RR, nor_163_out);
  nor nor_164 (nor_164_out, nor_163_out, nor_158_out);
  buf buffer_45 (buffer_45_out, nor_164_out);
  not not_15 (not_15_out, CLK_2);
  not not_16 (not_16_out, nand_9_out);
  or or_58 (or_58_out, nor_159_out, nor_126_out, nor_94_out, nor_47_out);
  or or_59 (or_59_out, nor_160_out, nor_127_out, nor_95_out, nor_48_out);
  or or_60 (DATA, or_63_out, buffer_46_out);
  buf buffer_46 (buffer_46_out, or_61_out);
  or or_61 (or_61_out, not_17_out, not_18_out);
  not not_17 (not_17_out, nand_10_out);
  not not_18 (not_18_out, nand_11_out);
  nand nand_10 (nand_10_out, RR, buffer_24_out);
  nand nand_11 (nand_11_out, buffer_45_out, buffer_25_out);
  buf buffer_47 (_15_RR, RR);
  nor nor_165 (nor_165_out, nor_168_out, nor_166_out);
  or or_62 (or_62_out, RST, nor_166_out);
  nor nor_166 (nor_166_out, nor_165_out, not_15_out);
  nor nor_167 (nor_167_out, nor_166_out, not_15_out, nor_168_out);
  nor nor_168 (nor_168_out, nor_167_out, not_16_out);
  or or_63 (or_63_out, or_58_out, or_59_out, or_43_out);
  nand nand_12 (nand_12_out, buffer_27_out, CLK_2);
  nor nor_169 (SKIP, or_62_out, nor_170_out);
  nor nor_170 (nor_170_out, SKIP, nor_167_out);
  buf buffer_48 (buffer_48_out, SKIP);
  nor nor_171 (nor_171_out, nor_174_out, nor_172_out);
  nor nor_172 (nor_172_out, nor_171_out, nand_12_out);
  nor nor_173 (nor_173_out, nor_172_out, nand_12_out, nor_174_out);
  nor nor_174 (nor_174_out, nor_173_out, DATA);
  nand nand_13 (nand_13_out, buffer_48_out, buffer_31_out);
  or or_64 (or_64_out, RST, nor_172_out);
  nor nor_175 (OEN, or_64_out, nor_176_out);
  nor nor_176 (nor_176_out, OEN, nor_173_out);
  not not_19 (not_19_out, nand_14_out);
  or or_65 (or_65_out, not_19_out, not_20_out);
  not not_20 (not_20_out, nand_13_out);
  nand nand_14 (nand_14_out, or_65_out, buffer_31_out);
  nand nand_15 (nand_15_out, nand_14_out, buffer_31_out);
  or or_66 (or_66_out, buffer_25_out, buffer_24_out);
  not not_21 (not_21_out, nand_15_out);
  nand nand_16 (nand_16_out, CLK_1, OEN, or_66_out);
  buf buffer_49 (_9_FLGF, not_21_out);
  not not_22 (_2_WRITE, nand_16_out);

  assign CLK_2_2 = CLK_2;
  assign DATA_2 = DATA;

  // Notes on the sheet:
  //   Single Step Panel
  //   EXTERNAL SWITCHES
  //   CLK1
  //   This is not how the actual clock is built.
  //   CLK2
  //   In reality, the clock is derived from the paper tape,
  //   and an analog RC delay is used to create CLK2.
  //   EXTERNAL PIN HEADER
  //   On the actual machine, this is a paper tape reader.
  //   There is no reset on the actual machine.
  //   This is required here to keep Logisim happy.
  //   0000: NOP
  //   0001: LD
  //   0010: ADD
  //   0011: SUB
  //   0100: ONE
  //   0101: NAND
  //   0110: OR
  //   0111: XOR
  //   1000: STO
  //   1001: STOC
  //   1010: IEN
  //   1011: OEN
  //   1100: JMP
  //   1101: RTN
  //   1110: SKZ
  //   1111: NOP
endmodule
