// Logisim project MSDFF.circ as structural Verilog: 1 circuit, main circuit main
module main (
  input  CLK,
  input  DATA,
  output out_3
);

  wire and_1_out, and_2_out, and_3_out, and_4_out, not_1_out, not_2_out, not_3_out, not_4_out, not_6_out,
       or_1_out, or_2_out, or_3_out, or_4_out;

  not not_1 (not_1_out, CLK);
  not not_2 (not_2_out, DATA);
  and and_1 (and_1_out, DATA, CLK);
  or or_1 (or_1_out, and_1_out, not_4_out);
  or or_2 (or_2_out, not_3_out, and_2_out);
  and and_2 (and_2_out, CLK, not_2_out);
  not not_3 (not_3_out, or_1_out);
  not not_4 (not_4_out, or_2_out);
  and and_3 (and_3_out, not_3_out, not_1_out);
  or or_3 (or_3_out, and_3_out, not_6_out);
  or or_4 (or_4_out, out_3, and_4_out);
  and and_4 (and_4_out, not_1_out, not_4_out);
  not not_5 (out_3, or_3_out);
  not not_6 (not_6_out, or_4_out);
endmodule
